// Logisim project 4_RISC_CPU.circ as structural Verilog: 9 circuits, main circuit main
module main (
  output [7:0] out_1
);

  wire Carry_q, CLK_out, not_1_out, not_2_out, RESET_out, ula_1_overflow, ula_1_zero,
       unidade_controle_1_clk_ac, unidade_controle_1_clk_ir, unidade_controle_1_clk_pc,
       unidade_controle_1_clk_ram, unidade_controle_1_dir, unidade_controle_1_e, unidade_controle_1_load,
       unidade_controle_1_r_nw, unidade_controle_1_rst_pc, Zero_q;
  wire [2:0] unidade_controle_1_opcode;
  wire [3:0] AC_q, multiplexer_1_out, PC_q, ram_1_data, ula_1_sa, unidade_controle_1_operand,
       unidade_controle_1_operand_pc;
  wire [7:0] rom_1_data;

  not not_1 (not_1_out, unidade_controle_1_load);
  Counter #(.width(4), .max('hf), .trigger("falling")) PC (
    .load(unidade_controle_1_load), .D(unidade_controle_1_operand_pc), .count(not_1_out), .Q(PC_q),
    .clk(unidade_controle_1_clk_pc), .clr(unidade_controle_1_rst_pc));  // open: carry
  unidade_controle unidade_controle_1 (
    .OPERAND(unidade_controle_1_operand), .DIR(unidade_controle_1_dir), .OPCODE(unidade_controle_1_opcode),
    .INSTRUCTION(out_1), .CLK_IR(unidade_controle_1_clk_ir), .CLK_RAM(unidade_controle_1_clk_ram),
    .CLK_AC(unidade_controle_1_clk_ac), .CLK_PC(unidade_controle_1_clk_pc),
    .RST_PC(unidade_controle_1_rst_pc), .CLK(CLK_out), .RESET(RESET_out), .ZERO(Zero_q),
    .OPERAND_PC(unidade_controle_1_operand_pc), .OVERFLOW(Carry_q), .LOAD(unidade_controle_1_load),
    .R_nW(unidade_controle_1_r_nw), .E(unidade_controle_1_e));
  Clock CLK (.out(CLK_out));
  Button RESET (.out(RESET_out));
  ROM #(.addrWidth(4)) rom_1 (.addr(PC_q), .data(rom_1_data));  // open: sel
  Register #(.trigger("high")) IR (.D(rom_1_data), .Q(out_1), .clk(unidade_controle_1_clk_ir));  // open: en, clr
  Multiplexer #(.width(4), .enable("false")) multiplexer_1 (
    .in0(unidade_controle_1_operand), .in1(ram_1_data), .out(multiplexer_1_out), .sel(unidade_controle_1_e));
  ULA ula_1 (
    .A(AC_q), .B(multiplexer_1_out), .OPCODE(unidade_controle_1_opcode), .OVERFLOW(ula_1_overflow),
    .\DIREÇÃO (unidade_controle_1_dir), .ZERO(ula_1_zero), .SA(ula_1_sa));
  Register #(.width(4)) AC (.D(ula_1_sa), .Q(AC_q), .clk(unidade_controle_1_clk_ac));  // open: en, clr
  D_Flip_Flop Carry (.clk(unidade_controle_1_clk_ac), .D(ula_1_overflow), .Q(Carry_q));  // open: Qn, preset, en, reset
  D_Flip_Flop Zero (.clk(unidade_controle_1_clk_ac), .D(ula_1_zero), .Q(Zero_q));  // open: Qn, preset, en, reset
  RAM #(.addrWidth(4), .dataWidth(4)) ram_1 (
    .addr(unidade_controle_1_operand), .data(ram_1_data), .clk(unidade_controle_1_clk_ram),
    .ld(unidade_controle_1_r_nw));  // open: sel, clr
  assign ram_1_data = not_2_out ? AC_q : 4'bz;  // Controlled_Buffer controlled_buffer_1
  not not_2 (not_2_out, unidade_controle_1_r_nw);

  // Notes on the sheet:
  //   1
  //   2
  //   3
  //   4
  //   5
  //   A
  //   D
  //   F
  //   MOV
  //   0
  //   000 0
  //   MOV
  //   000 1
  //   001 0
  //   ADD
  //   001 1
  //   ADD
  //   010 0
  //   SUB
  //   010 1
  //   SUB
  //   011 0
  //   OR
  //   6
  //   7
  //   011 1
  //   OR
  //   8
  //   100 0
  //   NOT
  //   9
  //   NOT
  //   100 1
  //   SHF
  //   101 0
  //   B
  //   SHF
  //   101 1
  //   JPZ
  //   110 0
  //   C
  //   110 1
  //   JPO
  //   111 0
  //   GO
  //   E
  //   111 1
  //   STR
  //   INSTRUCTION SET
  //   AC <= X
  //   AC <= M(X)
  //   AC <= AC + X
  //   AC <= AC + M(X)
  //   AC <= AC - X
  //   AC <= AC - M(X)
  //   AC <= AC OR X
  //   AC <= AC OR M(X)
  //   AC <= NOT X
  //   AC <= NOT M(X)
  //   AC <= AC << Q
  //   AC <= AC >> Q
  //   PC <= X SE FLAG Z
  //   PC <= X SE FLAG O
  //   PC <= X
  //   M(X) <= AC
  //   MEMORY PROGRAM
  //   contents of rom_1 (hex, n*v repeats v):
  //   0 f0 1 f1 10 31 d0 f2 11 f0 12 f1 e4
  //   4 BITS RISC CPU
  //   DATA MEMORY
endmodule

module somador_4_bits (
  input  [3:0] A,
  input  [3:0] B,
  input  VEM_1___TERRA,
  output OVERFLOW,
  output [3:0] \SAÍDA 
);

  wire somador_1_bit_2_vai_1, somador_1_bit_3_vai_1, somador_1_bit_4_vai_1;

  somador_1_bit somador_1_bit_1 (
    .SOMA(\SAÍDA [3]), .VAI_1(OVERFLOW), .A(A[3]), .B(B[3]), .VEM_1(somador_1_bit_2_vai_1));
  somador_1_bit somador_1_bit_2 (
    .SOMA(\SAÍDA [2]), .VAI_1(somador_1_bit_2_vai_1), .A(A[2]), .B(B[2]), .VEM_1(somador_1_bit_4_vai_1));
  somador_1_bit somador_1_bit_3 (
    .SOMA(\SAÍDA [0]), .VAI_1(somador_1_bit_3_vai_1), .A(A[0]), .B(B[0]), .VEM_1(VEM_1___TERRA));
  somador_1_bit somador_1_bit_4 (
    .SOMA(\SAÍDA [1]), .VAI_1(somador_1_bit_4_vai_1), .A(A[1]), .B(B[1]), .VEM_1(somador_1_bit_3_vai_1));
  // Probe on \SAÍDA 
  // Probe on A
  // Probe on B
endmodule

module somador_1_bit (
  input  A,
  input  B,
  input  VEM_1,
  output SOMA,
  output VAI_1
);

  wire and_1_out, and_2_out, and_3_out, xor_1_out;

  xor xor_1 (xor_1_out, A, B);
  and and_1 (and_1_out, A, B);
  and and_2 (and_2_out, A, VEM_1);
  and and_3 (and_3_out, B, VEM_1);
  xor xor_2 (SOMA, xor_1_out, VEM_1);
  or or_1 (VAI_1, and_1_out, and_2_out, and_3_out);
endmodule

module decoder_3x8 (
  input  [2:0] in_1,
  output S0,
  output S1,
  output S2,
  output S3,
  output S4,
  output S5,
  output S6,
  output S7
);

  and and_1 (S0, ~in_1[0], ~in_1[1], ~in_1[2]);  // AND_Gate
  and and_2 (S1, in_1[0], ~in_1[1], ~in_1[2]);  // AND_Gate
  and and_3 (S2, ~in_1[0], in_1[1], ~in_1[2]);  // AND_Gate
  and and_4 (S3, in_1[0], in_1[1], ~in_1[2]);  // AND_Gate
  and and_5 (S4, ~in_1[0], ~in_1[1], in_1[2]);  // AND_Gate
  and and_6 (S5, in_1[0], ~in_1[1], in_1[2]);  // AND_Gate
  and and_7 (S6, ~in_1[0], in_1[1], in_1[2]);  // AND_Gate
  and and_8 (S7, in_1[0], in_1[1], in_1[2]);
endmodule

module or_4_bits (
  input  [3:0] A,
  input  [3:0] B,
  output [3:0] out_3
);

  or or_1 (out_3[3], A[3], B[3]);
  or or_2 (out_3[2], A[2], B[2]);
  or or_3 (out_3[1], A[1], B[1]);
  or or_4 (out_3[0], A[0], B[0]);
endmodule

module ULA (
  input  \DIREÇÃO ,
  input  [3:0] A,
  input  [3:0] B,
  input  [2:0] OPCODE,
  output ZERO,
  output OVERFLOW,
  output [3:0] SA
);

  wire and_1_out, and_2_out, decoder_3x8_1_s0, decoder_3x8_1_s1, decoder_3x8_1_s2, decoder_3x8_1_s3,
       decoder_3x8_1_s4, decoder_3x8_1_s5, decoder_3x8_1_s6, decoder_3x8_1_s7, not_1_out,
       somador_4_bits_1_overflow, subtrator_4_bits_1_overflow;
  wire [3:0] controlled_buffer_5_out, or_4_bits_1_out_3, shifter_1_out, shifter_2_out,
       \somador_4_bits_1_saída , \subtrator_4_bits_1_saída ;

  decoder_3x8 decoder_3x8_1 (
    .S0(decoder_3x8_1_s0), .S1(decoder_3x8_1_s1), .S2(decoder_3x8_1_s2), .S3(decoder_3x8_1_s3),
    .S4(decoder_3x8_1_s4), .S5(decoder_3x8_1_s5), .S6(decoder_3x8_1_s6), .S7(decoder_3x8_1_s7), .in_1(OPCODE));
  assign SA = decoder_3x8_1_s0 ? B : 4'bz;  // Controlled_Buffer controlled_buffer_1
  nor nor_1 (ZERO, decoder_3x8_1_s7, decoder_3x8_1_s6, SA[3], SA[2], SA[1], SA[0]);
  somador_4_bits somador_4_bits_1 (
    .A(B), .B(A), .OVERFLOW(somador_4_bits_1_overflow), .\SAÍDA (\somador_4_bits_1_saída ),
    .VEM_1___TERRA(1'b0));
  assign SA = decoder_3x8_1_s1 ? \somador_4_bits_1_saída  : 4'bz;  // Controlled_Buffer controlled_buffer_2
  and and_1 (and_1_out, somador_4_bits_1_overflow, decoder_3x8_1_s1);
  and and_2 (and_2_out, decoder_3x8_1_s2, subtrator_4_bits_1_overflow);
  or or_1 (OVERFLOW, and_1_out, and_2_out);
  subtrator_4_bits subtrator_4_bits_1 (
    .A(A), .B(B), .OVERFLOW(subtrator_4_bits_1_overflow), .\SAÍDA (\subtrator_4_bits_1_saída ),
    .VEM_1___TERRA(1'b0));
  assign SA = decoder_3x8_1_s2 ? \subtrator_4_bits_1_saída  : 4'bz;  // Controlled_Buffer controlled_buffer_3
  or_4_bits or_4_bits_1 (.B(A), .A(B), .out_3(or_4_bits_1_out_3));
  assign SA = decoder_3x8_1_s3 ? or_4_bits_1_out_3 : 4'bz;  // Controlled_Buffer controlled_buffer_4
  assign SA = decoder_3x8_1_s4 ? ~B : 4'bz;  // Controlled_Inverter controlled_inverter_1
  not not_1 (not_1_out, \DIREÇÃO );
  Shifter #(.width(4)) shifter_1 (.in(A), .\dist (B[1:0]), .out(shifter_1_out));
  assign controlled_buffer_5_out = not_1_out ? shifter_1_out : 4'bz;  // Controlled_Buffer controlled_buffer_5
  Shifter #(.width(4), .shift("lr")) shifter_2 (.in(A), .\dist (B[1:0]), .out(shifter_2_out));
  assign controlled_buffer_5_out = \DIREÇÃO  ? shifter_2_out : 4'bz;  // Controlled_Buffer controlled_buffer_6
  assign SA = decoder_3x8_1_s5 ? controlled_buffer_5_out : 4'bz;  // Controlled_Buffer controlled_buffer_7
endmodule

module subtrator_1_bit (
  input  A,
  input  B,
  input  VEM_1,
  output SOMA,
  output VAI_1
);

  wire and_1_out, and_2_out, and_3_out, xor_1_out;

  xor xor_1 (xor_1_out, A, B);
  and and_1 (and_1_out, B, VEM_1);
  and and_2 (and_2_out, ~A, VEM_1);  // AND_Gate
  and and_3 (and_3_out, ~A, B);  // AND_Gate
  xor xor_2 (SOMA, xor_1_out, VEM_1);
  or or_1 (VAI_1, and_1_out, and_2_out, and_3_out);
endmodule

module subtrator_4_bits (
  input  [3:0] A,
  input  [3:0] B,
  input  VEM_1___TERRA,
  output OVERFLOW,
  output [3:0] \SAÍDA 
);

  wire subtrator_1_bit_2_vai_1, subtrator_1_bit_3_vai_1, subtrator_1_bit_4_vai_1;

  subtrator_1_bit subtrator_1_bit_1 (
    .SOMA(\SAÍDA [3]), .VAI_1(OVERFLOW), .A(A[3]), .B(B[3]), .VEM_1(subtrator_1_bit_2_vai_1));
  subtrator_1_bit subtrator_1_bit_2 (
    .SOMA(\SAÍDA [2]), .VAI_1(subtrator_1_bit_2_vai_1), .A(A[2]), .B(B[2]), .VEM_1(subtrator_1_bit_3_vai_1));
  subtrator_1_bit subtrator_1_bit_3 (
    .SOMA(\SAÍDA [1]), .VAI_1(subtrator_1_bit_3_vai_1), .A(A[1]), .B(B[1]), .VEM_1(subtrator_1_bit_4_vai_1));
  // Probe on \SAÍDA 
  subtrator_1_bit subtrator_1_bit_4 (
    .SOMA(\SAÍDA [0]), .VAI_1(subtrator_1_bit_4_vai_1), .A(A[0]), .B(B[0]), .VEM_1(VEM_1___TERRA));
  // Probe on A
  // Probe on B
endmodule

module unidade_controle (
  input  [7:0] INSTRUCTION,
  input  CLK,
  input  RESET,
  input  ZERO,
  input  OVERFLOW,
  output RST_PC,
  output CLK_IR,
  output CLK_AC,
  output CLK_RAM,
  output CLK_PC,
  output [3:0] OPERAND_PC,
  output [3:0] OPERAND,
  output DIR,
  output [2:0] OPCODE,
  output E,
  output R_nW,
  output LOAD
);

  wire and_1_out, GTO_out, JPO_out, JPZ_out;
  wire [1:0] counter_1_q;

  Counter #(.width(2), .max('h3)) counter_1 (.Q(counter_1_q), .clk(CLK), .clr(RESET));  // open: load, D, count, carry
  and and_1 (and_1_out, INSTRUCTION[5], ~INSTRUCTION[6], INSTRUCTION[7]);  // AND_Gate
  nand STR (R_nW, CLK_AC, INSTRUCTION[7], INSTRUCTION[6], INSTRUCTION[5], INSTRUCTION[4]);
  and and_2 (E, INSTRUCTION[4], ~and_1_out);  // AND_Gate
  and and_3 (CLK_RAM, counter_1_q[1], counter_1_q[0]);
  and and_4 (CLK_IR, ~counter_1_q[1], ~counter_1_q[0]);  // AND_Gate
  and GTO (GTO_out, CLK_PC, INSTRUCTION[7], INSTRUCTION[6], INSTRUCTION[5], ~INSTRUCTION[4]);  // AND_Gate
  and and_5 (CLK_AC, counter_1_q[1], ~counter_1_q[0]);  // AND_Gate
  and and_6 (CLK_PC, ~counter_1_q[1], counter_1_q[0]);  // AND_Gate
  and JPO (JPO_out, CLK_PC, INSTRUCTION[7], INSTRUCTION[6], ~INSTRUCTION[5], INSTRUCTION[4], OVERFLOW);  // AND_Gate
  or or_1 (LOAD, GTO_out, JPO_out, JPZ_out);
  and JPZ (JPZ_out, CLK_PC, INSTRUCTION[7], INSTRUCTION[6], ~INSTRUCTION[5], ~INSTRUCTION[4], ZERO);  // AND_Gate

  assign DIR = INSTRUCTION[4];
  assign OPCODE = INSTRUCTION[7:5];
  assign OPERAND = INSTRUCTION[3:0];
  assign OPERAND_PC = INSTRUCTION[3:0];
  assign RST_PC = RESET;
endmodule
